# Fritzing sketch receiver_arduino_wiring (saved by Fritzing 0.9.3b)
circuit board: 10.1776cm x 5.36194cm
breadboards: 1

parts:
  SBUS_RC = Dagu DGServo 9g header (male) [package=THT]
  NPN = NPN-Transistor [part_number=BC337 package="TO92 [THT]"]
  4_7kΩ = Resistor [tolerance=±5% resistance=4.7k package=THT]
  10kΩ = Resistor [tolerance=±5% resistance=10k package=THT]
  Arduino_MEGA_R3_Quadcopter_Shield = Arduino Mega 2560 (Rev3)

nets:
  GND: SBUS_RC.gnd, NPN.E, Arduino_MEGA_R3_Quadcopter_Shield.GND
  VCC: SBUS_RC.Vcc, 4_7kΩ.Pin_0, Arduino_MEGA_R3_Quadcopter_Shield.5V
  N1: SBUS_RC.pulse, 10kΩ.Pin_1
  N2: NPN.B, 10kΩ.Pin_0
  N3: NPN.C, 4_7kΩ.Pin_1, Arduino_MEGA_R3_Quadcopter_Shield.D19/RX1
