# Fritzing sketch arduino drone pcb Sketch (saved by Fritzing 0.9.3b)
circuit board: 10.1776cm x 5.36194cm
breadboards: 3

parts:
  Part1 = Arduino Mega 2560 (Rev3)
  Q1 = NPN-Transistor [part_number=BC337 package="TO92 [THT]"]
  Part2 = InvenSense MPU6050
  Motor_2 = Dagu DGServo 9g header (male) [package=THT]
  Motor_4 = Dagu DGServo 9g header (male) [package=THT]
  Motor_3 = Dagu DGServo 9g header (male) [package=THT]
  Motor_1 = Dagu DGServo 9g header (male) [package=THT]
  SBUS_RECEIVER = Dagu DGServo 9g header (male) [package=THT]
  R2 = Resistor [tolerance=±5% resistance=10k package="0805 [SMD]"]
  R1 = Resistor [tolerance=±5% resistance=4.7k package="0805 [SMD]"]
  J1 = female pin header, 7 pins [form="♀ (female)" part_number=ms5661]
  R3 = Resistor [tolerance=±5% resistance=220 package="0603 [SMD]"]
  R4 = Resistor [tolerance=±5% resistance=220 package="0603 [SMD]"]
  LED1 = LED - 5mm [color="Red (633nm)" package="5 mm [THT]"]
  buzzer = Piezo Speaker

nets:
  N1: Part1.D21/SCL, Part1.SCL, Part2.SCL, J1.pin3
  N2: Part1.D20/SDA, Part1.SDA, Part2.SDA, J1.pin4
  N3: Part1.D19/RX1, Q1.C, R1.Pin_1
  GND: Part1.GND, Q1.E, Part2.GND, Motor_2.gnd, Motor_4.gnd, Motor_3.gnd, Motor_1.gnd, SBUS_RECEIVER.gnd, J1.pin2, LED1.cathode, buzzer.pin1
  N4: Part1.D13_PWM, R3.Pin_1
  N5: Part1.D12_PWM, R4.Pin_1
  VCC: Part1.5V, Part2.VCC, Motor_2.Vcc, Motor_4.Vcc, Motor_3.Vcc, Motor_1.Vcc, SBUS_RECEIVER.Vcc, R1.Pin_0, J1.pin1
  N6: Part1.D2_PWM, Part2.INT
  N7: Part1.D4_PWM, Motor_4.pulse
  N8: Part1.D5_PWM, Motor_3.pulse
  N9: Part1.D6_PWM, Motor_2.pulse
  N10: Part1.D7_PWM, Motor_1.pulse
  N11: Q1.B, R2.Pin_0
  N12: SBUS_RECEIVER.pulse, R2.Pin_1
  N13: R3.Pin_0, LED1.anode
  N14: R4.Pin_0, buzzer.pin2
